// Logisim project fibonacci.circ as structural Verilog: 1 circuit, main circuit main
module main (
);

  wire cdm_16_1_p1, clock_2_out, mem, not_1_out, read, word;
  wire [15:0] address_bus, cdm_16_1_p2, cdm_16_1_p7, cdm_16_1_p8, data_bus;

  // CdM_16 cdm_16_1: pin names not known; wires that end beside it: cdm_16_1_p1, cdm_16_1_p2, mem, read, word, address_bus, cdm_16_1_p7, cdm_16_1_p8
  Clock clock_1 (.out(cdm_16_1_p1));
  LED led_1 (.in(cdm_16_1_p2[0]));
  assign data_bus = not_1_out ? cdm_16_1_p7 : 16'bz;  // Controlled_Buffer controlled_buffer_1
  not not_1 (not_1_out, read);
  assign cdm_16_1_p8 = read ? data_bus : 16'bz;  // Controlled_Buffer controlled_buffer_2
  // Debugger debugger_1: pin names not known
  Clock clock_2 (.out(clock_2_out));
  // RAM ram_1: pin names not known; wires that end beside it: address_bus, word, mem, clock_2_out, read, data_bus
endmodule
